# Fritzing sketch sketch agitatron (saved by Fritzing 0.9.3b)
breadboards: 1

parts:
  Componente1 = Arduino Nano (Rev3.0)
  S1 = Toggle Switch [package=THT]
  R1 = Rotary Potentiometer (Large) [maximum_resistance=10kΩ package=THT]
  R2 = Resistor [tolerance=±5% resistance=1k package="0402 [SMD]"]  # not connected
  R3 = Resistor [tolerance=±5% resistance=1k package="0402 [SMD]"]  # not connected
  J1 = Basic Servo

nets:
  N1: Componente1.D4, S1.L1
  N2: Componente1.D5, S1.L2
  GND: Componente1.GND, R1.leg1, J1.gnd
  5V: Componente1.5V, R1.leg2, J1.vcc
  N3: Componente1.A0, R1.wiper
